# Fritzing sketch Circuitry Diagram (saved by Fritzing 0.9.3b)
breadboards: 2

parts:
  Part1 = Arduino Mega 2560 (Rev3)
  U1 = L9110 H-bridge module [part_number="L9110 H-bridge"]
  U2 = L9110 H-bridge module [part_number="L9110 H-bridge"]
  U3 = L9110 H-bridge module [part_number="L9110 H-bridge"]
  U4 = L9110 H-bridge module [part_number="L9110 H-bridge"]
  M1 = Stepper Motor - Unipolar
  M2 = Stepper Motor - Unipolar
  M3 = Stepper Motor - Unipolar
  M4 = Stepper Motor - Unipolar
  S2 = Pushbutton [package="[THT]"]  # not connected
  S1 = Pushbutton [package="[THT]"]  # not connected
  S4 = Pushbutton [package="[THT]"]  # not connected
  LCD1 = LCD screen
  R1 = Rotary Potentiometer (Small) [maximum_resistance=100kΩ package=THT]

nets:
  N1: Part1.D15/RX3, U4.A-IB
  N2: Part1.D14/TX3, U4.A-IA
  N3: Part1.D13_PWM, U1.B-IA
  N4: Part1.D12_PWM, U1.B-IB
  N5: Part1.D11_PWM, U1.A-IA
  N6: Part1.D10_PWM, U1.A-IB
  N7: Part1.D9_PWM, U2.B-IA
  N8: Part1.D8_PWM, U2.B-IB
  VCC: Part1.5V, U1.VCC, U2.VCC, U3.VCC, U4.VCC, LCD1.VDD, LCD1.LED+, R1.leg1
  GND: Part1.GND, U1.GND, U2.GND, U3.GND, U4.GND, LCD1.VSS, LCD1.R/W, LCD1.LED-, R1.leg2
  N9: Part1.D0_RX0, U4.B-IB
  N10: Part1.D1_TX0, U4.B-IA
  N11: Part1.D2_PWM, U3.A-IB
  N12: Part1.D3_PWM, U3.A-IA
  N13: Part1.D4_PWM, U3.B-IB
  N14: Part1.D5_PWM, U3.B-IA
  N15: Part1.D6_PWM, U2.A-IB
  N16: Part1.D7_PWM, U2.A-IA
  N17: Part1.D35, LCD1.DB7
  N18: Part1.D37, LCD1.DB6
  N19: Part1.D39, LCD1.DB5
  N20: Part1.D41, LCD1.DB4
  N21: Part1.D43, LCD1.E
  N22: Part1.D45, LCD1.RS
  N23: U1.MOTOR_A-A, M1.D
  N24: U1.MOTOR_A-B, M1.COMMON_2
  N25: U1.MOTOR_B-A, M1.COMMON_1
  N26: U1.MOTOR_B-B, M1.A
  N27: U2.MOTOR_A-A, M2.D
  N28: U2.MOTOR_A-B, M2.B, M2.COMMON_2
  N29: U2.MOTOR_B-A, M2.COMMON_1
  N30: U2.MOTOR_B-B, M2.A
  N31: U3.MOTOR_A-A, M3.D
  N32: U3.MOTOR_A-B, M3.COMMON_2
  N33: U3.MOTOR_B-A, M3.COMMON_1
  N34: U3.MOTOR_B-B, M3.A
  N35: U4.MOTOR_A-A, M4.D
  N36: U4.MOTOR_A-B, M4.B, M4.COMMON_2
  N37: U4.MOTOR_B-A, M4.COMMON_1
  N38: U4.MOTOR_B-B, M4.A
  N39: LCD1.V0, R1.wiper
